# Fritzing sketch Blink (saved by Fritzing 0.9.4)
breadboards: 1

parts:
  MCU1 = Raspberry Pi Zero
  R1 = Resistor [tolerance=±5% resistance=330 package=THT]
  LED1 = LED - 5mm [color="Green (555nm)" package="5 mm [THT]"]

nets:
  N1: MCU1.pin_6, MCU1.pin_34, LED1.cathode
  N2: MCU1.pin_29, R1.Pin_0
  N3: R1.Pin_1, LED1.anode

notes:
  Circuito Elétrico de exemplo para o artigo "Como piscar um LED utilizando BananaPi e Python via SSH"no Medium.
  Henrique Otogami
  26/01/2025
